# Fritzing sketch SoilMoisture (saved by Fritzing 0.9.3b)
circuit board: 2.45147cm x 2.34762cm
breadboards: 1

parts:
  U2 = 555 Timer [package="SO8 [SMD]"]
  R1 = Resistor [tolerance=±5% resistance=220 package="0805 [SMD]"]
  R2 = Resistor [tolerance=±5% resistance=220 package="0805 [SMD]"]
  C1 = Ceramic Capacitor [capacitance=10nF package="0805 [SMD, multilayer]"]
  J1 = female pin header, 2 pins [form="♀ (female)"]
  J2 = female pin header, 1 pin [form="♀ (female)"]
  100nF = Ceramic Capacitor [capacitance=10nF package="0805 [SMD, multilayer]"]

nets:
  GND: U2.Pin_1, C1.0, J1.pin2, 100nF.0
  N1: U2.Pin_2, U2.Pin_6, R2.Pin_0, J1.pin1, 100nF.1
  N2: U2.Pin_3, J2.pin1
  5V: U2.Pin_4, U2.Pin_8, R1.Pin_1
  N3: U2.Pin_5, C1.1
  N4: U2.Pin_7, R1.Pin_0, R2.Pin_1
